# Fritzing sketch Skematik Sistem Pemantau + nRF + IoT (A) (saved by Fritzing 0.9.4)

parts:
  J1 = Camdenboss CTB0158-3 [part_number=CTB0158-3 package=THT]
  J2 = Camdenboss CTB0158-2 [part_number=CTB0158-2 package=THT]
  Part1 = Arduino Nano (Rev3.0) (ICSP)
  J3 = Camdenboss CTB0158-2 [part_number=CTB0158-2 package=THT]
  J4 = Camdenboss CTB0158-2 [part_number=CTB0158-2 package=THT]
  J5 = Camdenboss CTB0158-2 [part_number=CTB0158-2 package=THT]
  J6 = Camdenboss CTB0158-2 [part_number=CTB0158-2 package=THT]
  J7 = Camdenboss CTB0158-3 [part_number=CTB0158-3 package=THT]
  J8 = Camdenboss CTB0158-3 [part_number=CTB0158-3 package=THT]
  J9 = Camdenboss CTB0158-2 [part_number=CTB0158-2 package=THT]
  J10 = Camdenboss CTB0158-2 [part_number=CTB0158-2 package=THT]
  J11 = Camdenboss CTB0158-2 [part_number=CTB0158-2 package=THT]
  J12 = Camdenboss CTB0158-2 [part_number=CTB0158-2 package=THT]
  J13 = Camdenboss CTB0158-2 [part_number=CTB0158-2 package=THT]
  J14 = Camdenboss CTB0158-2 [part_number=CTB0158-2 package=THT]
  J15 = Camdenboss CTB0158-2 [part_number=CTB0158-2 package=THT]
  J16 = Camdenboss CTB0158-2 [part_number=CTB0158-2 package=THT]
  ZS-042_RTC1 = ZS-042 RTC Module
  J17 = Camdenboss CTB0158-3 [part_number=CTB0158-3 package=THT]
  U1 = 4-Channel 5v Relay Shield [package=relay-4ch5v10a]  # not connected
  M1 = NRF24L01-BO [package=THT]

nets:
  GND: J1.pin1, Part1.GND, J3.pin1, J5.pin1, J6.pin2, J9.pin1, J10.pin1, J11.pin1, J12.pin1, J13.pin1, J14.pin1, J15.pin1, ZS-042_RTC1.GND, M1.GND
  N1: J1.pin2, Part1.D7
  VCC: J1.pin3, Part1.VIN, J3.pin2, J5.pin2, J9.pin2, J10.pin2, J11.pin2, J12.pin2, J13.pin2, J14.pin2, J15.pin2, ZS-042_RTC1.VCC, M1.VCC
  N2: J2.pin1, Part1.A5, J4.pin1, ZS-042_RTC1.SCL
  N3: J2.pin2, Part1.A4, J4.pin2, ZS-042_RTC1.SDA
  N4: Part1.D2, J7.pin2
  N5: Part1.D3, J7.pin3
  N6: Part1.D4, J8.pin3
  N7: Part1.D5, J8.pin2
  N8: Part1.D6, J8.pin1
  N9: Part1.D8, J17.pin3
  N10: Part1.D9, M1.CE
  N11: Part1.D10, M1.CSN
  N12: Part1.D11/MOSI, M1.M0
  N13: Part1.D12/MISO, M1.M1
  N14: Part1.A7, J16.pin2
  N15: Part1.A6, J6.pin1
  N16: Part1.A2, J17.pin1
  N17: Part1.A1, J17.pin2
  N18: Part1.A0, J7.pin1
  N19: Part1.D13/SCK, M1.SCK

notes:
  SDA |A4 SCL |A5
  VCC |VCC
  GND |GND
  (LCD 20x4)
  OUT|GND
  A6|GND
  (Sensor pH)
  OUT|A7
  (Sensor Tekanan 2)
  SO|D4
  CS|D5
  SCK|D6
  (Termocouple)
  OUT|D3 (Sensor Air)
  OUT|D2 (Sensor Aliran Gas)
  OUT|A0 (Sensor Tekanan 1)
  VCC | IN1 | GND
  VCC | D7 | GND
  (Relay 4-Channel)
  SCL|SDA|VCC|GND
  A5 | A4 |VCC|GND
  (Real-Time Clock )
  GND
  VCC
  (Sumber Daya +5V)
  IN2 | IN3 | IN4
  D8 | A1 | A2
  (Relay 4-Channel)
  VCC
  GND
  (Sumber Daya +5V)
  Pompa Air
  Lampu Strobe
  Katup DC
  Motor AC
  VCC | IN4 | IN3 | IN2 | IN1 | GND
  CE |D9
  CSN |D10
  SCK |D13
  MOSI |D11
  MISO |D12
  IRQ |--
  (NRF24l01+PA+LNA)

custom parts:
  4-Channel 5v Relay Shield: 4 Channel 5v Relay Shield w. 2x SPD-06VDC-SD-C
  NRF24L01-BO: NRF24L01-BO breakout board for the NRF24L01. Pcb view suppressed as unneeded.
